# Fritzing sketch Sensor (saved by Fritzing 0.9.3b)
breadboards: 1

parts:
  U1 = NodeMCU V1.0
  VCC1 = 4 x AAA Battery Mount
  DS1 = DS18B20 [part_number=DS18B20]
  R1 = Resistor [tolerance=±5% resistance=470k package=THT]
  R2 = Resistor [tolerance=±5% resistance=470k package=THT]
  U2 = LM 358 Dual Op-Amp [part_number=LM358 package="DIP8 [THT]"]
  DHT1 = DHT22
  R3 = Resistor [tolerance=±5% resistance=4.7k package=THT]
  R4 = Resistor [tolerance=±5% resistance=4.7k package=THT]

nets:
  N1: U1.D1, DHT1.DATA, R4.Pin_1
  N2: U1.D3, DS1.DQ, R3.Pin_1
  VDD: U1.3V3, DS1.VDD, DHT1.VDD, R3.Pin_0, R4.Pin_0
  GND: U1.GND, VCC1.-, DS1.GND, R1.Pin_1, U2.connector3, DHT1.GND
  N3: U1.Vin, VCC1.+, R2.Pin_1, U2.connector7
  N4: U1.A0, U2.connector0, U2.connector1
  N5: R1.Pin_0, R2.Pin_0, U2.connector2

custom parts:
  NodeMCU V1.0: ESP8266 based NodeMCU
  DS18B20: DS18B20 1-Wire Temperature Sensor
  DHT22: DHT22 Humidity and Temperature Sensor
